# Fritzing sketch TinyGame (saved by Fritzing 0.9.2b)
circuit board: 3cm x 4cm
breadboards: 1

parts:
  R = Pushbutton [package="[THT]"]
  L = Pushbutton [package="[THT]"]
  100nF = Ceramic Capacitor [capacitance=100nF package="100 mil [THT, multilayer]"]
  Attiny85 = attiny85 [package=dip]
  10k = Resistor [tolerance=±5% resistance=10k package=THT]
  10k1 = Resistor [tolerance=±5% resistance=10k package=THT]
  CR2032 = CR2032
  BUZ = Piezo Speaker
  SSD1306 = female pin header, 4 pins [form="♀ (female)"]
  RST = Pushbutton [package="[THT]"]
  10k_2 = Resistor [tolerance=±5% resistance=10k package=THT]

nets:
  3.3V: R.Pin_1, R.Pin_2, L.Pin_3, L.Pin_4, 100nF.0, Attiny85.Pin_8, 10k.Pin_0, 10k1.Pin_0, CR2032.+, SSD1306.pin1, 10k_2.Pin_0
  N1: R.Pin_3, R.Pin_4, Attiny85.Pin_7
  N2: L.Pin_1, L.Pin_2, Attiny85.Pin_5
  GND: 100nF.1, Attiny85.Pin_4, 10k.Pin_1, 10k1.Pin_1, CR2032.-, BUZ.pin1, SSD1306.pin2, RST.Pin_1, RST.Pin_2
  N3: Attiny85.Pin_1, RST.Pin_3, RST.Pin_4, 10k_2.Pin_1
  N4: Attiny85.Pin_2, SSD1306.pin3
  N5: Attiny85.Pin_3, SSD1306.pin4
  N6: Attiny85.Pin_6, BUZ.pin2

notes:
  .
  gnd
  Based on the work of
  http://webboggles.com/attiny85-breakout-keychain-game/
  This version has been improved with the addition of reset button, this way it is possible to reset the system in case of an infinite loop or similar bug in the software.

custom parts:
  CR2032: CR2032 coin cell PCB adapter
